// Logisim project matchinggameproject.circ as structural Verilog: 1 circuit, main circuit main
module main (
);

  wire ACERTADO_00, ACERTADO_01, ACERTADO_02, ACERTADO_03, ACERTADO_10, ACERTADO_11, ACERTADO_12,
       ACERTADO_13, ACERTADO_20, ACERTADO_21, ACERTADO_22, ACERTADO_23, ACERTADO_30, ACERTADO_31,
       ACERTADO_32, ACERTADO_33, ACRT00, ACRT01, ACRT02, ACRT03, ACRT10, ACRT11, ACRT12, ACRT13, ACRT20,
       ACRT21, ACRT22, ACRT23, ACRT30, ACRT31, ACRT32, ACRT33, and_5_out, and_6_out, and_11_out, and_17_out,
       and_18_out, and_23_out, and_24_out, and_25_out, and_26_out, and_27_out, and_28_out, and_29_out,
       and_30_out, and_31_out, and_32_out, and_33_out, and_34_out, and_35_out, and_36_out, and_37_out,
       and_38_out, and_39_out, and_40_out, and_41_out, and_42_out, and_43_out, and_44_out, and_45_out,
       and_46_out, and_47_out, and_48_out, and_49_out, and_50_out, and_51_out, and_52_out, and_53_out,
       and_54_out, and_71_out, and_76_out, and_77_out, and_78_out, and_79_out, and_80_out, and_81_out,
       and_82_out, and_83_out, and_84_out, and_85_out, and_86_out, and_87_out, and_88_out, and_89_out,
       and_90_out, and_91_out, and_92_out, and_93_out, and_94_out, and_95_out, and_96_out, and_97_out,
       and_98_out, and_99_out, and_100_out, and_101_out, and_102_out, and_103_out, and_104_out, and_105_out,
       and_106_out, and_107_out, and_108_out, and_109_out, and_110_out, and_111_out, and_112_out,
       and_113_out, and_114_out, and_115_out, and_116_out, and_117_out, and_118_out, and_119_out,
       and_120_out, and_121_out, and_122_out, and_123_out, and_124_out, and_125_out, and_126_out,
       and_127_out, and_128_out, and_129_out, and_130_out, and_131_out, and_132_out, and_133_out,
       and_134_out, and_135_out, and_136_out, and_137_out, and_138_out, and_139_out, BOTAO_COLUNA,
       BOTAO_LINHA, CHECK, comparator_1_eq, comparator_2_eq, comparator_3_eq, comparator_4_eq,
       comparator_5_eq, comparator_6_eq, comparator_7_eq, comparator_8_eq, comparator_9_eq, comparator_10_eq,
       comparator_11_eq, comparator_12_eq, comparator_13_eq, comparator_14_eq, comparator_15_eq,
       comparator_16_eq, comparator_17_eq, comparator_18_eq, comparator_19_eq, comparator_20_eq,
       comparator_21_eq, comparator_22_eq, comparator_23_eq, comparator_24_eq, comparator_25_eq,
       comparator_26_eq, comparator_27_eq, comparator_28_eq, comparator_29_eq, comparator_30_eq,
       comparator_31_eq, comparator_32_eq, comparator_33_eq, comparator_34_eq, comparator_35_eq,
       comparator_36_eq, comparator_37_eq, comparator_38_eq, comparator_39_eq, comparator_40_eq,
       comparator_41_eq, comparator_42_eq, comparator_43_eq, comparator_44_eq, comparator_45_eq,
       comparator_46_eq, comparator_47_eq, comparator_48_eq, comparator_49_eq, comparator_50_eq,
       comparator_51_eq, comparator_52_eq, comparator_53_eq, comparator_54_eq, comparator_55_eq,
       comparator_56_eq, comparator_57_eq, comparator_58_eq, comparator_59_eq, comparator_60_eq,
       comparator_61_eq, comparator_62_eq, comparator_63_eq, comparator_64_eq, comparator_65_eq,
       comparator_66_eq, comparator_67_eq, comparator_68_eq, comparator_69_eq, comparator_70_eq,
       comparator_71_eq, comparator_72_eq, comparator_73_eq, comparator_74_eq, comparator_75_eq,
       comparator_76_eq, comparator_77_eq, comparator_78_eq, comparator_79_eq, comparator_80_eq,
       comparator_81_eq, comparator_82_eq, comparator_83_eq, comparator_84_eq, comparator_85_eq,
       comparator_86_eq, comparator_87_eq, comparator_88_eq, comparator_89_eq, comparator_90_eq,
       comparator_91_eq, comparator_92_eq, comparator_93_eq, comparator_94_eq, comparator_95_eq,
       comparator_96_eq, comparator_97_eq, comparator_98_eq, comparator_99_eq, comparator_100_eq,
       comparator_101_eq, comparator_102_eq, comparator_103_eq, comparator_104_eq, comparator_105_eq,
       comparator_106_eq, comparator_107_eq, comparator_108_eq, comparator_109_eq, comparator_110_eq,
       comparator_111_eq, comparator_112_eq, comparator_113_eq, comparator_114_eq, comparator_115_eq,
       comparator_116_eq, comparator_117_eq, comparator_118_eq, comparator_119_eq, comparator_120_eq,
       comparator_121_eq, comparator_122_eq, comparator_123_eq, comparator_124_eq, comparator_125_eq,
       comparator_126_eq, comparator_127_eq, comparator_128_eq, comparator_129_eq, comparator_130_eq,
       comparator_131_eq, comparator_132_eq, comparator_133_eq, comparator_134_eq, comparator_135_eq,
       comparator_136_eq, comparator_137_eq, comparator_138_eq, comparator_139_eq, comparator_140_eq,
       comparator_141_eq, comparator_142_eq, comparator_143_eq, comparator_144_eq, comparator_145_eq,
       comparator_146_eq, comparator_147_eq, comparator_148_eq, comparator_149_eq, comparator_150_eq,
       comparator_151_eq, comparator_152_eq, comparator_153_eq, comparator_154_eq, comparator_155_eq,
       comparator_156_eq, comparator_157_eq, comparator_158_eq, comparator_159_eq, comparator_160_eq,
       comparator_161_eq, comparator_162_eq, comparator_163_eq, comparator_164_eq, comparator_165_eq,
       CONFIRMA, ESTADO_0, ESTADO_1, ESTADO_2, ESTADO_3, J1, J2, L00, L01, L02, L03, L10, L11, L12, L13, L20,
       L21, L22, L23, L30, L31, L32, L33, multiplexer_1_out, MUX00, MUX01, MUX02, MUX03, MUX10, MUX11, MUX12,
       MUX13, MUX20, MUX21, MUX22, MUX23, MUX30, MUX31, MUX32, MUX33, not_1_out, not_2_out, not_3_out,
       not_4_out, or_1_out, or_2_out, or_3_out, or_4_out, or_5_out, or_6_out, or_7_out, or_8_out, or_9_out,
       or_10_out, or_11_out, or_12_out, or_13_out, or_14_out, or_15_out, or_16_out, or_17_out;
  wire [1:0] COLUNA, COLUNA_1, COLUNA_2, counter_3_q, LINHA, LINHA_1, LINHA_2;
  wire [3:0] multiplexer_2_out, multiplexer_3_out, PONTJ1, PONTJ2, V00, V01, V02, V03, V10, V11, V12, V13,
       V20, V21, V22, V23, V30, V31, V32, V33;

  Button button_1 (.out(BOTAO_LINHA));
  Button button_2 (.out(BOTAO_COLUNA));
  Button button_3 (.out(CONFIRMA));
  Counter #(.width(2), .max('h3)) counter_1 (.Q(LINHA), .clk(BOTAO_LINHA));  // open: load, D, count, carry, clr
  Counter #(.width(2), .max('h3)) counter_2 (.Q(COLUNA), .clk(BOTAO_COLUNA));  // open: load, D, count, carry, clr
  Multiplexer #(.select(4)) multiplexer_1 (
    .in0(ACRT00), .in1(ACRT01), .in2(ACRT02), .in3(ACRT03), .in4(ACRT10), .in5(ACRT11), .in6(ACRT12),
    .in7(ACRT13), .in8(ACRT20), .in9(ACRT21), .in10(ACRT22), .in11(ACRT23), .in12(ACRT30), .in13(ACRT31),
    .in14(ACRT32), .in15(ACRT33), .out(multiplexer_1_out), .sel({LINHA, COLUNA}));  // open: en
  Multiplexer #(.select(4), .width(4), .enable("false")) multiplexer_2 (
    .in0(4'b1000), .in1(4'b0110), .in2(4'b1110), .in3(4'b0011), .in4(4'b1110), .in5(4'b1111), .in6(4'b0001),
    .in7(4'b1010), .in8(4'b0010), .in9(4'b0010), .in10(4'b0011), .in11(4'b0001), .in12(4'b0110),
    .in13(4'b1010), .in14(4'b1000), .in15(4'b1111), .out(multiplexer_2_out), .sel({LINHA_1, COLUNA_1}));
  Multiplexer #(.select(4), .width(4), .enable("false")) multiplexer_3 (
    .in0(4'b1000), .in1(4'b0110), .in2(4'b1110), .in3(4'b0011), .in4(4'b1110), .in5(4'b1111), .in6(4'b0001),
    .in7(4'b1010), .in8(4'b0010), .in9(4'b0010), .in10(4'b0011), .in11(4'b0001), .in12(4'b0110),
    .in13(4'b1010), .in14(4'b1000), .in15(4'b1111), .out(multiplexer_3_out), .sel({LINHA_2, COLUNA_2}));
  LED led_1 (.in(L00));
  Hex_Digit_Display hex_digit_display_1 (.value(V00));  // open: dp
  LED led_2 (.in(L10));
  Hex_Digit_Display hex_digit_display_2 (.value(V10));  // open: dp
  LED led_3 (.in(L20));
  Hex_Digit_Display hex_digit_display_3 (.value(V20));  // open: dp
  LED led_4 (.in(L30));
  Hex_Digit_Display hex_digit_display_4 (.value(V30));  // open: dp
  Comparator #(.width(2)) comparator_1 (.a(LINHA), .b(2'b00), .eq(comparator_1_eq));  // open: gt, lt
  Comparator #(.width(2)) comparator_2 (.a(COLUNA), .b(2'b00), .eq(comparator_2_eq));  // open: gt, lt
  Comparator #(.width(2)) comparator_3 (.a(LINHA), .b(2'b01), .eq(comparator_3_eq));  // open: gt, lt
  Comparator #(.width(2)) comparator_4 (.a(COLUNA), .b(2'b00), .eq(comparator_4_eq));  // open: gt, lt
  Comparator #(.width(2)) comparator_5 (.a(LINHA), .b(2'b10), .eq(comparator_5_eq));  // open: gt, lt
  Comparator #(.width(2)) comparator_6 (.a(COLUNA), .b(2'b00), .eq(comparator_6_eq));  // open: gt, lt
  Comparator #(.width(2)) comparator_7 (.a(LINHA), .b(2'b11), .eq(comparator_7_eq));  // open: gt, lt
  Comparator #(.width(2)) comparator_8 (.a(COLUNA), .b(2'b00), .eq(comparator_8_eq));  // open: gt, lt
  LED led_5 (.in(L01));
  Hex_Digit_Display hex_digit_display_5 (.value(V01));  // open: dp
  LED led_6 (.in(L11));
  Hex_Digit_Display hex_digit_display_6 (.value(V11));  // open: dp
  LED led_7 (.in(L21));
  Hex_Digit_Display hex_digit_display_7 (.value(V21));  // open: dp
  LED led_8 (.in(L31));
  Hex_Digit_Display hex_digit_display_8 (.value(V31));  // open: dp
  and and_1 (L00, comparator_1_eq, comparator_2_eq);
  and and_2 (L10, comparator_3_eq, comparator_4_eq);
  and and_3 (L20, comparator_5_eq, comparator_6_eq);
  and and_4 (L30, comparator_7_eq, comparator_8_eq);
  Counter #(.width(2), .max('h3)) counter_3 (
    .Q(counter_3_q), .clk(and_5_out), .clr(ESTADO_3));  // open: load, D, count, carry
  and and_5 (and_5_out, ~multiplexer_1_out, ~and_6_out, CONFIRMA);  // AND_Gate
  and and_6 (and_6_out, ESTADO_1, comparator_9_eq, comparator_10_eq);
  Comparator #(.width(2)) comparator_9 (.a(COLUNA), .b(COLUNA_1), .eq(comparator_9_eq));  // open: gt, lt
  Comparator #(.width(2)) comparator_10 (.a(LINHA), .b(LINHA_1), .eq(comparator_10_eq));  // open: gt, lt
  Comparator #(.width(4)) comparator_11 (
    .a(multiplexer_2_out), .b(multiplexer_3_out), .eq(comparator_11_eq));  // open: gt, lt
  LED led_9 (.in(L02));
  Hex_Digit_Display hex_digit_display_9 (.value(V02));  // open: dp
  LED led_10 (.in(L12));
  Hex_Digit_Display hex_digit_display_10 (.value(V12));  // open: dp
  LED led_11 (.in(L22));
  Hex_Digit_Display hex_digit_display_11 (.value(V22));  // open: dp
  LED led_12 (.in(L32));
  Hex_Digit_Display hex_digit_display_12 (.value(V32));  // open: dp
  Comparator #(.width(2)) comparator_12 (.a(COLUNA_2), .b(COLUNA_1), .eq(comparator_12_eq));  // open: gt, lt
  Comparator #(.width(2)) comparator_13 (.a(LINHA_2), .b(LINHA_1), .eq(comparator_13_eq));  // open: gt, lt
  and and_7 (ESTADO_0, ~counter_3_q[0], ~counter_3_q[1]);  // AND_Gate
  and and_8 (ESTADO_1, counter_3_q[0], ~counter_3_q[1]);  // AND_Gate
  and and_9 (ESTADO_2, ~counter_3_q[0], counter_3_q[1]);  // AND_Gate
  and and_10 (ESTADO_3, counter_3_q[0], counter_3_q[1]);
  or or_1 (or_1_out, ~comparator_12_eq, ~comparator_13_eq);  // OR_Gate
  LED led_13 (.in(L03));
  Hex_Digit_Display hex_digit_display_13 (.value(V03));  // open: dp
  LED led_14 (.in(L13));
  Hex_Digit_Display hex_digit_display_14 (.value(V13));  // open: dp
  LED led_15 (.in(L23));
  Hex_Digit_Display hex_digit_display_15 (.value(V23));  // open: dp
  LED led_16 (.in(L33));
  Hex_Digit_Display hex_digit_display_16 (.value(V33));  // open: dp
  Comparator #(.width(2)) comparator_14 (.a(LINHA), .b(2'b00), .eq(comparator_14_eq));  // open: gt, lt
  Comparator #(.width(2)) comparator_15 (.a(COLUNA), .b(2'b01), .eq(comparator_15_eq));  // open: gt, lt
  Comparator #(.width(2)) comparator_16 (.a(LINHA), .b(2'b01), .eq(comparator_16_eq));  // open: gt, lt
  Comparator #(.width(2)) comparator_17 (.a(COLUNA), .b(2'b01), .eq(comparator_17_eq));  // open: gt, lt
  Comparator #(.width(2)) comparator_18 (.a(LINHA), .b(2'b10), .eq(comparator_18_eq));  // open: gt, lt
  Comparator #(.width(2)) comparator_19 (.a(COLUNA), .b(2'b01), .eq(comparator_19_eq));  // open: gt, lt
  Comparator #(.width(2)) comparator_20 (.a(LINHA), .b(2'b11), .eq(comparator_20_eq));  // open: gt, lt
  Comparator #(.width(2)) comparator_21 (.a(COLUNA), .b(2'b01), .eq(comparator_21_eq));  // open: gt, lt
  and and_11 (and_11_out, not_1_out, CHECK);
  not not_1 (not_1_out, not_2_out);
  not not_2 (not_2_out, J1);
  and and_12 (CHECK, or_1_out, comparator_11_eq, ESTADO_3);
  and and_13 (L01, comparator_14_eq, comparator_15_eq);
  and and_14 (L11, comparator_16_eq, comparator_17_eq);
  and and_15 (L21, comparator_18_eq, comparator_19_eq);
  and and_16 (L31, comparator_20_eq, comparator_21_eq);
  Counter #(.width(4), .max('hf), .ongoal("load")) counter_4 (
    .Q(PONTJ1), .clk(and_11_out));  // open: load, D, count, carry, clr
  LED led_17 (.in(J1));
  Hex_Digit_Display hex_digit_display_17 (.value(PONTJ1));  // open: dp
  Counter #(.width(4), .max('hf), .ongoal("load")) counter_5 (
    .Q(PONTJ2), .clk(and_17_out));  // open: load, D, count, carry, clr
  and and_17 (and_17_out, CHECK, not_3_out);
  not not_3 (not_3_out, not_4_out);
  not not_4 (not_4_out, J2);
  LED led_18 (.in(J2));
  Hex_Digit_Display hex_digit_display_18 (.value(PONTJ2));  // open: dp
  LED led_19 (.in(ESTADO_0));
  Comparator #(.width(2)) comparator_22 (.a(LINHA), .b(2'b00), .eq(comparator_22_eq));  // open: gt, lt
  Comparator #(.width(2)) comparator_23 (.a(COLUNA), .b(2'b10), .eq(comparator_23_eq));  // open: gt, lt
  Comparator #(.width(2)) comparator_24 (.a(LINHA), .b(2'b01), .eq(comparator_24_eq));  // open: gt, lt
  Comparator #(.width(2)) comparator_25 (.a(COLUNA), .b(2'b10), .eq(comparator_25_eq));  // open: gt, lt
  Comparator #(.width(2)) comparator_26 (.a(LINHA), .b(2'b10), .eq(comparator_26_eq));  // open: gt, lt
  Comparator #(.width(2)) comparator_27 (.a(COLUNA), .b(2'b10), .eq(comparator_27_eq));  // open: gt, lt
  Comparator #(.width(2)) comparator_28 (.a(LINHA), .b(2'b11), .eq(comparator_28_eq));  // open: gt, lt
  Comparator #(.width(2)) comparator_29 (.a(COLUNA), .b(2'b10), .eq(comparator_29_eq));  // open: gt, lt
  and and_18 (and_18_out, CONFIRMA, ESTADO_0);
  LED led_20 (.in(ESTADO_1));
  and and_19 (L02, comparator_22_eq, comparator_23_eq);
  and and_20 (L12, comparator_24_eq, comparator_25_eq);
  and and_21 (L22, comparator_26_eq, comparator_27_eq);
  and and_22 (L32, comparator_28_eq, comparator_29_eq);
  Register #(.width(2)) register_1 (.D(LINHA), .Q(LINHA_1), .clk(and_18_out));  // open: en, clr
  Register #(.width(2)) register_2 (.D(COLUNA), .Q(COLUNA_1), .clk(and_18_out));  // open: en, clr
  Comparator #(.width(2)) comparator_30 (.a(LINHA_1), .b(2'b00), .eq(comparator_30_eq));  // open: gt, lt
  and and_23 (and_23_out, comparator_30_eq, comparator_31_eq);
  Comparator #(.width(2)) comparator_31 (.a(COLUNA_1), .b(2'b00), .eq(comparator_31_eq));  // open: gt, lt
  Comparator #(.width(2)) comparator_32 (.a(LINHA_2), .b(2'b00), .eq(comparator_32_eq));  // open: gt, lt
  and and_24 (and_24_out, comparator_32_eq, comparator_33_eq);
  Comparator #(.width(2)) comparator_33 (.a(COLUNA_2), .b(2'b00), .eq(comparator_33_eq));  // open: gt, lt
  Comparator #(.width(2)) comparator_34 (.a(LINHA_1), .b(2'b00), .eq(comparator_34_eq));  // open: gt, lt
  and and_25 (and_25_out, comparator_34_eq, comparator_35_eq);
  Comparator #(.width(2)) comparator_35 (.a(COLUNA_1), .b(2'b01), .eq(comparator_35_eq));  // open: gt, lt
  Comparator #(.width(2)) comparator_36 (.a(LINHA_2), .b(2'b00), .eq(comparator_36_eq));  // open: gt, lt
  and and_26 (and_26_out, comparator_36_eq, comparator_37_eq);
  Comparator #(.width(2)) comparator_37 (.a(COLUNA_2), .b(2'b01), .eq(comparator_37_eq));  // open: gt, lt
  Comparator #(.width(2)) comparator_38 (.a(LINHA_1), .b(2'b00), .eq(comparator_38_eq));  // open: gt, lt
  and and_27 (and_27_out, comparator_38_eq, comparator_39_eq);
  Comparator #(.width(2)) comparator_39 (.a(COLUNA_1), .b(2'b10), .eq(comparator_39_eq));  // open: gt, lt
  Comparator #(.width(2)) comparator_40 (.a(LINHA_2), .b(2'b00), .eq(comparator_40_eq));  // open: gt, lt
  and and_28 (and_28_out, comparator_40_eq, comparator_41_eq);
  Comparator #(.width(2)) comparator_41 (.a(COLUNA_2), .b(2'b10), .eq(comparator_41_eq));  // open: gt, lt
  Comparator #(.width(2)) comparator_42 (.a(LINHA_1), .b(2'b00), .eq(comparator_42_eq));  // open: gt, lt
  and and_29 (and_29_out, comparator_42_eq, comparator_43_eq);
  Comparator #(.width(2)) comparator_43 (.a(COLUNA_1), .b(2'b11), .eq(comparator_43_eq));  // open: gt, lt
  Comparator #(.width(2)) comparator_44 (.a(LINHA_2), .b(2'b00), .eq(comparator_44_eq));  // open: gt, lt
  and and_30 (and_30_out, comparator_44_eq, comparator_45_eq);
  Comparator #(.width(2)) comparator_45 (.a(COLUNA_2), .b(2'b11), .eq(comparator_45_eq));  // open: gt, lt
  Comparator #(.width(2)) comparator_46 (.a(LINHA_1), .b(2'b01), .eq(comparator_46_eq));  // open: gt, lt
  and and_31 (and_31_out, comparator_46_eq, comparator_47_eq);
  Comparator #(.width(2)) comparator_47 (.a(COLUNA_1), .b(2'b00), .eq(comparator_47_eq));  // open: gt, lt
  Comparator #(.width(2)) comparator_48 (.a(LINHA_2), .b(2'b01), .eq(comparator_48_eq));  // open: gt, lt
  and and_32 (and_32_out, comparator_48_eq, comparator_49_eq);
  Comparator #(.width(2)) comparator_49 (.a(COLUNA_2), .b(2'b00), .eq(comparator_49_eq));  // open: gt, lt
  Comparator #(.width(2)) comparator_50 (.a(LINHA_1), .b(2'b01), .eq(comparator_50_eq));  // open: gt, lt
  and and_33 (and_33_out, comparator_50_eq, comparator_51_eq);
  Comparator #(.width(2)) comparator_51 (.a(COLUNA_1), .b(2'b01), .eq(comparator_51_eq));  // open: gt, lt
  Comparator #(.width(2)) comparator_52 (.a(LINHA_2), .b(2'b01), .eq(comparator_52_eq));  // open: gt, lt
  and and_34 (and_34_out, comparator_52_eq, comparator_53_eq);
  Comparator #(.width(2)) comparator_53 (.a(COLUNA_2), .b(2'b01), .eq(comparator_53_eq));  // open: gt, lt
  Comparator #(.width(2)) comparator_54 (.a(LINHA_1), .b(2'b01), .eq(comparator_54_eq));  // open: gt, lt
  and and_35 (and_35_out, comparator_54_eq, comparator_55_eq);
  Comparator #(.width(2)) comparator_55 (.a(COLUNA_1), .b(2'b10), .eq(comparator_55_eq));  // open: gt, lt
  Comparator #(.width(2)) comparator_56 (.a(LINHA_2), .b(2'b01), .eq(comparator_56_eq));  // open: gt, lt
  and and_36 (and_36_out, comparator_56_eq, comparator_57_eq);
  Comparator #(.width(2)) comparator_57 (.a(COLUNA_2), .b(2'b10), .eq(comparator_57_eq));  // open: gt, lt
  Comparator #(.width(2)) comparator_58 (.a(LINHA_1), .b(2'b01), .eq(comparator_58_eq));  // open: gt, lt
  and and_37 (and_37_out, comparator_58_eq, comparator_59_eq);
  Comparator #(.width(2)) comparator_59 (.a(COLUNA_1), .b(2'b11), .eq(comparator_59_eq));  // open: gt, lt
  Comparator #(.width(2)) comparator_60 (.a(LINHA_2), .b(2'b01), .eq(comparator_60_eq));  // open: gt, lt
  and and_38 (and_38_out, comparator_60_eq, comparator_61_eq);
  Comparator #(.width(2)) comparator_61 (.a(COLUNA_2), .b(2'b11), .eq(comparator_61_eq));  // open: gt, lt
  Comparator #(.width(2)) comparator_62 (.a(LINHA_1), .b(2'b10), .eq(comparator_62_eq));  // open: gt, lt
  and and_39 (and_39_out, comparator_62_eq, comparator_63_eq);
  Comparator #(.width(2)) comparator_63 (.a(COLUNA_1), .b(2'b00), .eq(comparator_63_eq));  // open: gt, lt
  Comparator #(.width(2)) comparator_64 (.a(LINHA_2), .b(2'b10), .eq(comparator_64_eq));  // open: gt, lt
  and and_40 (and_40_out, comparator_64_eq, comparator_65_eq);
  Comparator #(.width(2)) comparator_65 (.a(COLUNA_2), .b(2'b00), .eq(comparator_65_eq));  // open: gt, lt
  Comparator #(.width(2)) comparator_66 (.a(LINHA_1), .b(2'b10), .eq(comparator_66_eq));  // open: gt, lt
  and and_41 (and_41_out, comparator_66_eq, comparator_67_eq);
  Comparator #(.width(2)) comparator_67 (.a(COLUNA_1), .b(2'b01), .eq(comparator_67_eq));  // open: gt, lt
  Comparator #(.width(2)) comparator_68 (.a(LINHA_2), .b(2'b10), .eq(comparator_68_eq));  // open: gt, lt
  and and_42 (and_42_out, comparator_68_eq, comparator_69_eq);
  Comparator #(.width(2)) comparator_69 (.a(COLUNA_2), .b(2'b01), .eq(comparator_69_eq));  // open: gt, lt
  Comparator #(.width(2)) comparator_70 (.a(LINHA_1), .b(2'b10), .eq(comparator_70_eq));  // open: gt, lt
  and and_43 (and_43_out, comparator_70_eq, comparator_71_eq);
  Comparator #(.width(2)) comparator_71 (.a(COLUNA_1), .b(2'b10), .eq(comparator_71_eq));  // open: gt, lt
  Comparator #(.width(2)) comparator_72 (.a(LINHA_2), .b(2'b10), .eq(comparator_72_eq));  // open: gt, lt
  and and_44 (and_44_out, comparator_72_eq, comparator_73_eq);
  Comparator #(.width(2)) comparator_73 (.a(COLUNA_2), .b(2'b10), .eq(comparator_73_eq));  // open: gt, lt
  Comparator #(.width(2)) comparator_74 (.a(LINHA_1), .b(2'b10), .eq(comparator_74_eq));  // open: gt, lt
  and and_45 (and_45_out, comparator_74_eq, comparator_75_eq);
  Comparator #(.width(2)) comparator_75 (.a(COLUNA_1), .b(2'b11), .eq(comparator_75_eq));  // open: gt, lt
  Comparator #(.width(2)) comparator_76 (.a(LINHA_2), .b(2'b10), .eq(comparator_76_eq));  // open: gt, lt
  and and_46 (and_46_out, comparator_76_eq, comparator_77_eq);
  Comparator #(.width(2)) comparator_77 (.a(COLUNA_2), .b(2'b11), .eq(comparator_77_eq));  // open: gt, lt
  Comparator #(.width(2)) comparator_78 (.a(LINHA_1), .b(2'b11), .eq(comparator_78_eq));  // open: gt, lt
  and and_47 (and_47_out, comparator_78_eq, comparator_79_eq);
  Comparator #(.width(2)) comparator_79 (.a(COLUNA_1), .b(2'b00), .eq(comparator_79_eq));  // open: gt, lt
  Comparator #(.width(2)) comparator_80 (.a(LINHA_2), .b(2'b11), .eq(comparator_80_eq));  // open: gt, lt
  and and_48 (and_48_out, comparator_80_eq, comparator_81_eq);
  Comparator #(.width(2)) comparator_81 (.a(COLUNA_2), .b(2'b00), .eq(comparator_81_eq));  // open: gt, lt
  Comparator #(.width(2)) comparator_82 (.a(LINHA_1), .b(2'b11), .eq(comparator_82_eq));  // open: gt, lt
  and and_49 (and_49_out, comparator_82_eq, comparator_83_eq);
  Comparator #(.width(2)) comparator_83 (.a(COLUNA_1), .b(2'b01), .eq(comparator_83_eq));  // open: gt, lt
  Comparator #(.width(2)) comparator_84 (.a(LINHA_2), .b(2'b11), .eq(comparator_84_eq));  // open: gt, lt
  and and_50 (and_50_out, comparator_84_eq, comparator_85_eq);
  Comparator #(.width(2)) comparator_85 (.a(COLUNA_2), .b(2'b01), .eq(comparator_85_eq));  // open: gt, lt
  Comparator #(.width(2)) comparator_86 (.a(LINHA_1), .b(2'b11), .eq(comparator_86_eq));  // open: gt, lt
  and and_51 (and_51_out, comparator_86_eq, comparator_87_eq);
  Comparator #(.width(2)) comparator_87 (.a(COLUNA_1), .b(2'b10), .eq(comparator_87_eq));  // open: gt, lt
  Comparator #(.width(2)) comparator_88 (.a(LINHA_2), .b(2'b11), .eq(comparator_88_eq));  // open: gt, lt
  and and_52 (and_52_out, comparator_88_eq, comparator_89_eq);
  Comparator #(.width(2)) comparator_89 (.a(COLUNA_2), .b(2'b10), .eq(comparator_89_eq));  // open: gt, lt
  Comparator #(.width(2)) comparator_90 (.a(LINHA_1), .b(2'b11), .eq(comparator_90_eq));  // open: gt, lt
  and and_53 (and_53_out, comparator_90_eq, comparator_91_eq);
  Comparator #(.width(2)) comparator_91 (.a(COLUNA_1), .b(2'b11), .eq(comparator_91_eq));  // open: gt, lt
  Comparator #(.width(2)) comparator_92 (.a(LINHA_2), .b(2'b11), .eq(comparator_92_eq));  // open: gt, lt
  and and_54 (and_54_out, comparator_92_eq, comparator_93_eq);
  Comparator #(.width(2)) comparator_93 (.a(COLUNA_2), .b(2'b11), .eq(comparator_93_eq));  // open: gt, lt
  LED led_21 (.in(ESTADO_2));
  or or_2 (or_2_out, and_23_out, and_24_out);
  or or_3 (or_3_out, and_25_out, and_26_out);
  or or_4 (or_4_out, and_27_out, and_28_out);
  or or_5 (or_5_out, and_29_out, and_30_out);
  or or_6 (or_6_out, and_31_out, and_32_out);
  or or_7 (or_7_out, and_33_out, and_34_out);
  or or_8 (or_8_out, and_35_out, and_36_out);
  or or_9 (or_9_out, and_37_out, and_38_out);
  or or_10 (or_10_out, and_39_out, and_40_out);
  or or_11 (or_11_out, and_41_out, and_42_out);
  or or_12 (or_12_out, and_43_out, and_44_out);
  or or_13 (or_13_out, and_45_out, and_46_out);
  or or_14 (or_14_out, and_47_out, and_48_out);
  or or_15 (or_15_out, and_49_out, and_50_out);
  or or_16 (or_16_out, and_51_out, and_52_out);
  or or_17 (or_17_out, and_53_out, and_54_out);
  LED led_22 (.in(ESTADO_3));
  and and_55 (ACERTADO_00, CHECK, or_2_out);
  and and_56 (ACERTADO_01, CHECK, or_3_out);
  and and_57 (ACERTADO_02, CHECK, or_4_out);
  and and_58 (ACERTADO_03, CHECK, or_5_out);
  and and_59 (ACERTADO_10, CHECK, or_6_out);
  and and_60 (ACERTADO_11, CHECK, or_7_out);
  and and_61 (ACERTADO_12, CHECK, or_8_out);
  and and_62 (ACERTADO_13, CHECK, or_9_out);
  and and_63 (ACERTADO_20, CHECK, or_10_out);
  and and_64 (ACERTADO_21, CHECK, or_11_out);
  and and_65 (ACERTADO_22, CHECK, or_12_out);
  and and_66 (ACERTADO_23, CHECK, or_13_out);
  and and_67 (ACERTADO_30, CHECK, or_14_out);
  and and_68 (ACERTADO_31, CHECK, or_15_out);
  and and_69 (ACERTADO_32, CHECK, or_16_out);
  and and_70 (ACERTADO_33, CHECK, or_17_out);
  and and_71 (and_71_out, CONFIRMA, ESTADO_1);
  Comparator #(.width(2)) comparator_94 (.a(LINHA), .b(2'b00), .eq(comparator_94_eq));  // open: gt, lt
  Comparator #(.width(2)) comparator_95 (.a(COLUNA), .b(2'b11), .eq(comparator_95_eq));  // open: gt, lt
  Comparator #(.width(2)) comparator_96 (.a(LINHA), .b(2'b01), .eq(comparator_96_eq));  // open: gt, lt
  Comparator #(.width(2)) comparator_97 (.a(COLUNA), .b(2'b11), .eq(comparator_97_eq));  // open: gt, lt
  Comparator #(.width(2)) comparator_98 (.a(LINHA), .b(2'b10), .eq(comparator_98_eq));  // open: gt, lt
  Comparator #(.width(2)) comparator_99 (.a(COLUNA), .b(2'b11), .eq(comparator_99_eq));  // open: gt, lt
  Comparator #(.width(2)) comparator_100 (.a(LINHA), .b(2'b11), .eq(comparator_100_eq));  // open: gt, lt
  Comparator #(.width(2)) comparator_101 (.a(COLUNA), .b(2'b11), .eq(comparator_101_eq));  // open: gt, lt
  Register #(.width(2)) register_3 (.D(LINHA), .Q(LINHA_2), .clk(and_71_out));  // open: en, clr
  Register #(.width(2)) register_4 (.D(COLUNA), .Q(COLUNA_2), .clk(and_71_out));  // open: en, clr
  and and_72 (L03, comparator_94_eq, comparator_95_eq);
  and and_73 (L13, comparator_96_eq, comparator_97_eq);
  and and_74 (L23, comparator_98_eq, comparator_99_eq);
  and and_75 (L33, comparator_100_eq, comparator_101_eq);
  Multiplexer #(.width(4)) multiplexer_4 (.in1(4'b0001), .out(V23), .sel(MUX23));  // open: in0, en
  Multiplexer #(.width(4)) multiplexer_5 (.in1(4'b0010), .out(V20), .sel(MUX20));  // open: in0, en
  Multiplexer #(.width(4)) multiplexer_6 (.in1(4'b0011), .out(V22), .sel(MUX22));  // open: in0, en
  Multiplexer #(.width(4)) multiplexer_7 (.in1(4'b1010), .out(V31), .sel(MUX31));  // open: in0, en
  Comparator #(.width(2)) comparator_102 (.a(LINHA_2), .b(2'b00), .eq(comparator_102_eq));  // open: gt, lt
  Comparator #(.width(2)) comparator_103 (.a(COLUNA_2), .b(2'b00), .eq(comparator_103_eq));  // open: gt, lt
  Comparator #(.width(2)) comparator_104 (.a(LINHA_1), .b(2'b00), .eq(comparator_104_eq));  // open: gt, lt
  Comparator #(.width(2)) comparator_105 (.a(COLUNA_1), .b(2'b00), .eq(comparator_105_eq));  // open: gt, lt
  Comparator #(.width(2)) comparator_106 (.a(LINHA_2), .b(2'b01), .eq(comparator_106_eq));  // open: gt, lt
  Comparator #(.width(2)) comparator_107 (.a(COLUNA_2), .b(2'b00), .eq(comparator_107_eq));  // open: gt, lt
  Comparator #(.width(2)) comparator_108 (.a(LINHA_1), .b(2'b01), .eq(comparator_108_eq));  // open: gt, lt
  Comparator #(.width(2)) comparator_109 (.a(COLUNA_1), .b(2'b00), .eq(comparator_109_eq));  // open: gt, lt
  Comparator #(.width(2)) comparator_110 (.a(LINHA_2), .b(2'b10), .eq(comparator_110_eq));  // open: gt, lt
  Comparator #(.width(2)) comparator_111 (.a(COLUNA_2), .b(2'b00), .eq(comparator_111_eq));  // open: gt, lt
  Comparator #(.width(2)) comparator_112 (.a(LINHA_1), .b(2'b10), .eq(comparator_112_eq));  // open: gt, lt
  Comparator #(.width(2)) comparator_113 (.a(COLUNA_1), .b(2'b00), .eq(comparator_113_eq));  // open: gt, lt
  Comparator #(.width(2)) comparator_114 (.a(LINHA_2), .b(2'b11), .eq(comparator_114_eq));  // open: gt, lt
  Comparator #(.width(2)) comparator_115 (.a(COLUNA_2), .b(2'b00), .eq(comparator_115_eq));  // open: gt, lt
  Comparator #(.width(2)) comparator_116 (.a(LINHA_1), .b(2'b11), .eq(comparator_116_eq));  // open: gt, lt
  Comparator #(.width(2)) comparator_117 (.a(COLUNA_1), .b(2'b00), .eq(comparator_117_eq));  // open: gt, lt
  Multiplexer #(.width(4)) multiplexer_8 (.in1(4'b0001), .out(V12), .sel(MUX12));  // open: in0, en
  Multiplexer #(.width(4)) multiplexer_9 (.in1(4'b0010), .out(V21), .sel(MUX21));  // open: in0, en
  Multiplexer #(.width(4)) multiplexer_10 (.in1(4'b0011), .out(V03), .sel(MUX03));  // open: in0, en
  Multiplexer #(.width(4)) multiplexer_11 (.in1(4'b1010), .out(V13), .sel(MUX13));  // open: in0, en
  and and_76 (and_76_out, ESTADO_2, and_77_out);
  and and_77 (and_77_out, comparator_102_eq, comparator_103_eq);
  and and_78 (and_78_out, ~ESTADO_0, and_79_out);  // AND_Gate
  and and_79 (and_79_out, comparator_104_eq, comparator_105_eq);
  Register #(.width(1)) register_5 (.D(ACERTADO_00), .Q(ACRT00), .clk(ACERTADO_00));  // open: en, clr
  and and_80 (and_80_out, ESTADO_2, and_81_out);
  and and_81 (and_81_out, comparator_106_eq, comparator_107_eq);
  and and_82 (and_82_out, ~ESTADO_0, and_83_out);  // AND_Gate
  and and_83 (and_83_out, comparator_108_eq, comparator_109_eq);
  Register #(.width(1)) register_6 (.D(ACERTADO_10), .Q(ACRT10), .clk(ACERTADO_10));  // open: en, clr
  and and_84 (and_84_out, ESTADO_2, and_85_out);
  and and_85 (and_85_out, comparator_110_eq, comparator_111_eq);
  and and_86 (and_86_out, ~ESTADO_0, and_87_out);  // AND_Gate
  and and_87 (and_87_out, comparator_112_eq, comparator_113_eq);
  Register #(.width(1)) register_7 (.D(ACERTADO_20), .Q(ACRT20), .clk(ACERTADO_20));  // open: en, clr
  and and_88 (and_88_out, ESTADO_2, and_89_out);
  and and_89 (and_89_out, comparator_114_eq, comparator_115_eq);
  and and_90 (and_90_out, ~ESTADO_0, and_91_out);  // AND_Gate
  and and_91 (and_91_out, comparator_116_eq, comparator_117_eq);
  Register #(.width(1)) register_8 (.D(ACERTADO_30), .Q(ACRT30), .clk(ACERTADO_30));  // open: en, clr
  Multiplexer #(.width(4)) multiplexer_12 (.in1(4'b1111), .out(V11), .sel(MUX11));  // open: in0, en
  Multiplexer #(.width(4)) multiplexer_13 (.in1(4'b0110), .out(V01), .sel(MUX01));  // open: in0, en
  Multiplexer #(.width(4)) multiplexer_14 (.in1(4'b1000), .out(V32), .sel(MUX32));  // open: in0, en
  Multiplexer #(.width(4)) multiplexer_15 (.in1(4'b1110), .out(V10), .sel(MUX10));  // open: in0, en
  or or_18 (MUX00, and_76_out, and_78_out, ACRT00);
  or or_19 (MUX10, and_80_out, and_82_out, ACRT10);
  or or_20 (MUX20, and_84_out, and_86_out, ACRT20);
  or or_21 (MUX30, and_88_out, and_90_out, ACRT30);
  Multiplexer #(.width(4)) multiplexer_16 (.in1(4'b1111), .out(V33), .sel(MUX33));  // open: in0, en
  Multiplexer #(.width(4)) multiplexer_17 (.in1(4'b0110), .out(V30), .sel(MUX30));  // open: in0, en
  Multiplexer #(.width(4)) multiplexer_18 (.in1(4'b1000), .out(V00), .sel(MUX00));  // open: in0, en
  Multiplexer #(.width(4)) multiplexer_19 (.in1(4'b1110), .out(V02), .sel(MUX02));  // open: in0, en
  Comparator #(.width(2)) comparator_118 (.a(LINHA_2), .b(2'b00), .eq(comparator_118_eq));  // open: gt, lt
  Comparator #(.width(2)) comparator_119 (.a(COLUNA_2), .b(2'b01), .eq(comparator_119_eq));  // open: gt, lt
  Comparator #(.width(2)) comparator_120 (.a(LINHA_1), .b(2'b00), .eq(comparator_120_eq));  // open: gt, lt
  Comparator #(.width(2)) comparator_121 (.a(COLUNA_1), .b(2'b01), .eq(comparator_121_eq));  // open: gt, lt
  Comparator #(.width(2)) comparator_122 (.a(LINHA_2), .b(2'b01), .eq(comparator_122_eq));  // open: gt, lt
  Comparator #(.width(2)) comparator_123 (.a(COLUNA_2), .b(2'b01), .eq(comparator_123_eq));  // open: gt, lt
  Comparator #(.width(2)) comparator_124 (.a(LINHA_1), .b(2'b01), .eq(comparator_124_eq));  // open: gt, lt
  Comparator #(.width(2)) comparator_125 (.a(COLUNA_1), .b(2'b01), .eq(comparator_125_eq));  // open: gt, lt
  Comparator #(.width(2)) comparator_126 (.a(LINHA_2), .b(2'b10), .eq(comparator_126_eq));  // open: gt, lt
  Comparator #(.width(2)) comparator_127 (.a(COLUNA_2), .b(2'b01), .eq(comparator_127_eq));  // open: gt, lt
  Comparator #(.width(2)) comparator_128 (.a(LINHA_1), .b(2'b10), .eq(comparator_128_eq));  // open: gt, lt
  Comparator #(.width(2)) comparator_129 (.a(COLUNA_1), .b(2'b01), .eq(comparator_129_eq));  // open: gt, lt
  Comparator #(.width(2)) comparator_130 (.a(LINHA_2), .b(2'b11), .eq(comparator_130_eq));  // open: gt, lt
  Comparator #(.width(2)) comparator_131 (.a(COLUNA_2), .b(2'b01), .eq(comparator_131_eq));  // open: gt, lt
  Comparator #(.width(2)) comparator_132 (.a(LINHA_1), .b(2'b11), .eq(comparator_132_eq));  // open: gt, lt
  Comparator #(.width(2)) comparator_133 (.a(COLUNA_1), .b(2'b01), .eq(comparator_133_eq));  // open: gt, lt
  and and_92 (and_92_out, ESTADO_2, and_93_out);
  and and_93 (and_93_out, comparator_118_eq, comparator_119_eq);
  and and_94 (and_94_out, ~ESTADO_0, and_95_out);  // AND_Gate
  and and_95 (and_95_out, comparator_120_eq, comparator_121_eq);
  Register #(.width(1)) register_9 (.D(ACERTADO_01), .Q(ACRT01), .clk(ACERTADO_01));  // open: en, clr
  and and_96 (and_96_out, ESTADO_2, and_97_out);
  and and_97 (and_97_out, comparator_122_eq, comparator_123_eq);
  and and_98 (and_98_out, ~ESTADO_0, and_99_out);  // AND_Gate
  and and_99 (and_99_out, comparator_124_eq, comparator_125_eq);
  Register #(.width(1)) register_10 (.D(ACERTADO_11), .Q(ACRT11), .clk(ACERTADO_11));  // open: en, clr
  and and_100 (and_100_out, ESTADO_2, and_101_out);
  and and_101 (and_101_out, comparator_126_eq, comparator_127_eq);
  and and_102 (and_102_out, ~ESTADO_0, and_103_out);  // AND_Gate
  and and_103 (and_103_out, comparator_128_eq, comparator_129_eq);
  Register #(.width(1)) register_11 (.D(ACERTADO_21), .Q(ACRT21), .clk(ACERTADO_21));  // open: en, clr
  and and_104 (and_104_out, ESTADO_2, and_105_out);
  and and_105 (and_105_out, comparator_130_eq, comparator_131_eq);
  and and_106 (and_106_out, ~ESTADO_0, and_107_out);  // AND_Gate
  and and_107 (and_107_out, comparator_132_eq, comparator_133_eq);
  Register #(.width(1)) register_12 (.D(ACERTADO_31), .Q(ACRT31), .clk(ACERTADO_31));  // open: en, clr
  or or_22 (MUX01, and_92_out, and_94_out, ACRT01);
  or or_23 (MUX11, and_96_out, and_98_out, ACRT11);
  or or_24 (MUX21, and_100_out, and_102_out, ACRT21);
  or or_25 (MUX31, and_104_out, and_106_out, ACRT31);
  not not_5 (J1, J2);
  Counter #(.width(1), .max('h1)) counter_6 (.Q(J2), .clk(ESTADO_3));  // open: load, D, count, carry, clr
  Comparator #(.width(2)) comparator_134 (.a(LINHA_2), .b(2'b00), .eq(comparator_134_eq));  // open: gt, lt
  Comparator #(.width(2)) comparator_135 (.a(COLUNA_2), .b(2'b10), .eq(comparator_135_eq));  // open: gt, lt
  Comparator #(.width(2)) comparator_136 (.a(LINHA_1), .b(2'b00), .eq(comparator_136_eq));  // open: gt, lt
  Comparator #(.width(2)) comparator_137 (.a(COLUNA_1), .b(2'b10), .eq(comparator_137_eq));  // open: gt, lt
  Comparator #(.width(2)) comparator_138 (.a(LINHA_2), .b(2'b01), .eq(comparator_138_eq));  // open: gt, lt
  Comparator #(.width(2)) comparator_139 (.a(COLUNA_2), .b(2'b10), .eq(comparator_139_eq));  // open: gt, lt
  Comparator #(.width(2)) comparator_140 (.a(LINHA_1), .b(2'b01), .eq(comparator_140_eq));  // open: gt, lt
  Comparator #(.width(2)) comparator_141 (.a(COLUNA_1), .b(2'b10), .eq(comparator_141_eq));  // open: gt, lt
  Comparator #(.width(2)) comparator_142 (.a(LINHA_2), .b(2'b10), .eq(comparator_142_eq));  // open: gt, lt
  Comparator #(.width(2)) comparator_143 (.a(COLUNA_2), .b(2'b10), .eq(comparator_143_eq));  // open: gt, lt
  Comparator #(.width(2)) comparator_144 (.a(LINHA_1), .b(2'b10), .eq(comparator_144_eq));  // open: gt, lt
  Comparator #(.width(2)) comparator_145 (.a(COLUNA_1), .b(2'b10), .eq(comparator_145_eq));  // open: gt, lt
  Comparator #(.width(2)) comparator_146 (.a(LINHA_2), .b(2'b11), .eq(comparator_146_eq));  // open: gt, lt
  Comparator #(.width(2)) comparator_147 (.a(COLUNA_2), .b(2'b10), .eq(comparator_147_eq));  // open: gt, lt
  Comparator #(.width(2)) comparator_148 (.a(LINHA_1), .b(2'b11), .eq(comparator_148_eq));  // open: gt, lt
  Comparator #(.width(2)) comparator_149 (.a(COLUNA_1), .b(2'b10), .eq(comparator_149_eq));  // open: gt, lt
  and and_108 (and_108_out, ESTADO_2, and_109_out);
  and and_109 (and_109_out, comparator_134_eq, comparator_135_eq);
  and and_110 (and_110_out, ~ESTADO_0, and_111_out);  // AND_Gate
  and and_111 (and_111_out, comparator_136_eq, comparator_137_eq);
  Register #(.width(1)) register_13 (.D(ACERTADO_02), .Q(ACRT02), .clk(ACERTADO_02));  // open: en, clr
  and and_112 (and_112_out, ESTADO_2, and_113_out);
  and and_113 (and_113_out, comparator_138_eq, comparator_139_eq);
  and and_114 (and_114_out, ~ESTADO_0, and_115_out);  // AND_Gate
  and and_115 (and_115_out, comparator_140_eq, comparator_141_eq);
  Register #(.width(1)) register_14 (.D(ACERTADO_12), .Q(ACRT12), .clk(ACERTADO_12));  // open: en, clr
  and and_116 (and_116_out, ESTADO_2, and_117_out);
  and and_117 (and_117_out, comparator_142_eq, comparator_143_eq);
  and and_118 (and_118_out, ~ESTADO_0, and_119_out);  // AND_Gate
  and and_119 (and_119_out, comparator_144_eq, comparator_145_eq);
  Register #(.width(1)) register_15 (.D(ACERTADO_22), .Q(ACRT22), .clk(ACERTADO_22));  // open: en, clr
  and and_120 (and_120_out, ESTADO_2, and_121_out);
  and and_121 (and_121_out, comparator_146_eq, comparator_147_eq);
  and and_122 (and_122_out, ~ESTADO_0, and_123_out);  // AND_Gate
  and and_123 (and_123_out, comparator_148_eq, comparator_149_eq);
  Register #(.width(1)) register_16 (.D(ACERTADO_32), .Q(ACRT32), .clk(ACERTADO_32));  // open: en, clr
  or or_26 (MUX02, and_108_out, and_110_out, ACRT02);
  or or_27 (MUX12, and_112_out, and_114_out, ACRT12);
  or or_28 (MUX22, and_116_out, and_118_out, ACRT22);
  or or_29 (MUX32, and_120_out, and_122_out, ACRT32);
  Comparator #(.width(2)) comparator_150 (.a(LINHA_2), .b(2'b00), .eq(comparator_150_eq));  // open: gt, lt
  Comparator #(.width(2)) comparator_151 (.a(COLUNA_2), .b(2'b11), .eq(comparator_151_eq));  // open: gt, lt
  Comparator #(.width(2)) comparator_152 (.a(LINHA_1), .b(2'b00), .eq(comparator_152_eq));  // open: gt, lt
  Comparator #(.width(2)) comparator_153 (.a(COLUNA_1), .b(2'b11), .eq(comparator_153_eq));  // open: gt, lt
  Comparator #(.width(2)) comparator_154 (.a(LINHA_2), .b(2'b01), .eq(comparator_154_eq));  // open: gt, lt
  Comparator #(.width(2)) comparator_155 (.a(COLUNA_2), .b(2'b11), .eq(comparator_155_eq));  // open: gt, lt
  Comparator #(.width(2)) comparator_156 (.a(LINHA_1), .b(2'b01), .eq(comparator_156_eq));  // open: gt, lt
  Comparator #(.width(2)) comparator_157 (.a(COLUNA_1), .b(2'b11), .eq(comparator_157_eq));  // open: gt, lt
  Comparator #(.width(2)) comparator_158 (.a(LINHA_2), .b(2'b10), .eq(comparator_158_eq));  // open: gt, lt
  Comparator #(.width(2)) comparator_159 (.a(COLUNA_2), .b(2'b11), .eq(comparator_159_eq));  // open: gt, lt
  Comparator #(.width(2)) comparator_160 (.a(LINHA_1), .b(2'b10), .eq(comparator_160_eq));  // open: gt, lt
  Comparator #(.width(2)) comparator_161 (.a(COLUNA_1), .b(2'b11), .eq(comparator_161_eq));  // open: gt, lt
  Comparator #(.width(2)) comparator_162 (.a(LINHA_2), .b(2'b11), .eq(comparator_162_eq));  // open: gt, lt
  Comparator #(.width(2)) comparator_163 (.a(COLUNA_2), .b(2'b11), .eq(comparator_163_eq));  // open: gt, lt
  Comparator #(.width(2)) comparator_164 (.a(LINHA_1), .b(2'b11), .eq(comparator_164_eq));  // open: gt, lt
  Comparator #(.width(2)) comparator_165 (.a(COLUNA_1), .b(2'b11), .eq(comparator_165_eq));  // open: gt, lt
  and and_124 (and_124_out, ESTADO_2, and_125_out);
  and and_125 (and_125_out, comparator_150_eq, comparator_151_eq);
  and and_126 (and_126_out, ~ESTADO_0, and_127_out);  // AND_Gate
  and and_127 (and_127_out, comparator_152_eq, comparator_153_eq);
  Register #(.width(1)) register_17 (.D(ACERTADO_03), .Q(ACRT03), .clk(ACERTADO_03));  // open: en, clr
  and and_128 (and_128_out, ESTADO_2, and_129_out);
  and and_129 (and_129_out, comparator_154_eq, comparator_155_eq);
  and and_130 (and_130_out, ~ESTADO_0, and_131_out);  // AND_Gate
  and and_131 (and_131_out, comparator_156_eq, comparator_157_eq);
  Register #(.width(1)) register_18 (.D(ACERTADO_13), .Q(ACRT13), .clk(ACERTADO_13));  // open: en, clr
  and and_132 (and_132_out, ESTADO_2, and_133_out);
  and and_133 (and_133_out, comparator_158_eq, comparator_159_eq);
  and and_134 (and_134_out, ~ESTADO_0, and_135_out);  // AND_Gate
  and and_135 (and_135_out, comparator_160_eq, comparator_161_eq);
  Register #(.width(1)) register_19 (.D(ACERTADO_23), .Q(ACRT23), .clk(ACERTADO_23));  // open: en, clr
  and and_136 (and_136_out, ESTADO_2, and_137_out);
  and and_137 (and_137_out, comparator_162_eq, comparator_163_eq);
  and and_138 (and_138_out, ~ESTADO_0, and_139_out);  // AND_Gate
  and and_139 (and_139_out, comparator_164_eq, comparator_165_eq);
  Register #(.width(1)) register_20 (.D(ACERTADO_33), .Q(ACRT33), .clk(ACERTADO_33));  // open: en, clr
  or or_30 (MUX03, and_124_out, and_126_out, ACRT03);
  or or_31 (MUX13, and_128_out, and_130_out, ACRT13);
  or or_32 (MUX23, and_132_out, and_134_out, ACRT23);
  or or_33 (MUX33, and_136_out, and_138_out, ACRT33);

  // Notes on the sheet:
  //   SELEÇÃO DA LINHA E COLUNA:
  //   COMPARAÇÃO DAS ESCOLHAS:
  //   JOGO DA MEMÓRIA
  //   ESTADOS:
  //   J1
  //   J2
  //   REGISTRADOR DE LINHAS E COLUNAS:
  //   MOSTRAR DISPLAY:
  //   EMABARALHAMENTO DOS NÚMEROS:
  //   TROCA DE JOGADORES:
endmodule
